# Fritzing sketch station_meteo (saved by Fritzing 0.8.7b)
breadboards: 1

parts:
  RHT1 = Humidity and Temperature Sensor RHT03
  S1 = Pushbutton [package="[THT]"]
  S2 = Pushbutton [package="[THT]"]
  Part1 = Arduino Uno (Rev3)
  R2 = Photocell (LDR) [package=THT]
  R3 = Resistor [tolerance=±1% resistance=10k package=THT]
  R5 = Resistor [tolerance=±1% resistance=10k package=THT]
  R6 = Resistor [tolerance=±1% resistance=10k package=THT]
  LCD1 = LCD screen

nets:
  5V/G4: RHT1.Vcc, S1.Pin_3, S1.Pin_4, S2.Pin_3, S2.Pin_4, Part1.5V, R3.Pin_1, LCD1.VDD, LCD1.LED+
  G13: RHT1.Data-signal, Part1.D10_PWM/SS
  GND: RHT1.GND_2, Part1.GND, R2.pin_0, R5.Pin_1, R6.Pin_1, LCD1.VSS, LCD1.V0, LCD1.R/W, LCD1.LED-
  G34: S1.Pin_1, S1.Pin_2, Part1.D11_PWM/MOSI, R6.Pin_0
  G35: S2.Pin_1, S2.Pin_2, Part1.D12/MISO, R5.Pin_0
  G12: Part1.A0, R2.pin_1, R3.Pin_0
  G32: Part1.D2, LCD1.RS
  G33: Part1.D3_PWM, LCD1.E
  G25: Part1.D4, LCD1.DB4
  G26: Part1.D5_PWM, LCD1.DB5
  G27: Part1.D6_PWM, LCD1.DB6
  G14: Part1.D7, LCD1.DB7

notes:
  G13
  G34
  G35
  G12
  G32
  G33
  G25
  G26
  G27
  G14
  arduino
  esp32
